# Fritzing sketch ESP32_Boards (saved by Fritzing 0.9.10b)

parts:
  A1 = DORHEA ESP32 GPIO breakout board 30pin
  CPU1 = NodeMCU WROOM ESP 32  # not connected
  L298N1 = L298N DC motor driver
  VCC1 = Battery block 9V  # not connected
  WATER_PUMP1 = water pump/motor  # not connected
  DHT1 = DHT11 Humitidy and Temperature Sensor (3 pins)

nets:
  N1: A1.Pin_13, A1.Pin_52, DHT1.Signal
  N2: A1.Pin_26, DHT1.Plus
  N3: A1.Pin_37, A1.Pin_39, DHT1.Gnd
  N4: A1.Pin_69, A1.Pin_116, L298N1.ENA
  N5: A1.Pin_70, A1.Pin_117, L298N1.IN1
  N6: A1.Pin_73, A1.Pin_120, L298N1.IN2
  N7: A1.Pin_74, A1.Pin_121, L298N1.IN3
  N8: A1.Pin_75, A1.Pin_122, L298N1.IN4
  N9: A1.Pin_76, A1.Pin_123, L298N1.ENB

custom parts:
  DORHEA ESP32 GPIO breakout board 30pin: ESP32 shield 30P expansion board, supports two power supply : DC 6.5-16v and USB 5.V
  NodeMCU WROOM ESP 32: 30 pol Development Kit
  L298N DC motor driver: 2x DC motor driver with 78M05 positive voltage regulator (7..35 V) L298N: max 46 V, 2 A Set 5 V Enable jumper to enable 5 V regultor (needed for the L298N) and +5 V output at screw terminal or supply external +5 V at screw terminal Set ENA and/or ENB to +5 V to enable motor permanently or supply ENA and/or ENB with PWM signal IN1 and IN2 set rotation directory for motor A (OUT1/OUT2) IN2 and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
  water pump/motor: WATER PUMP BY ARDUBLOCKTR
  DHT11 Humitidy and Temperature Sensor (3 pins): DHT11 Humidity and Temperature Sensor (3 pins).
